// Logisim project RISC_V_16I_integrated_mem_inter.circ as structural Verilog: 24 circuits, main circuit carry_look
module carry_look (
  input  C,
  input  G0,
  input  P0,
  input  G1,
  input  P1,
  input  G2,
  input  P2,
  input  G3,
  input  P3,
  output C1,
  output C2,
  output C3,
  output GG,
  output GP
);

  wire C_P0_out, G0_P1_out, G1_P2_out, G2_P3_out, or_1_out, or_2_out, or_4_out, P0_P1_out, P1_out, P2_2_out,
       P2_out, P2_P3_out, P3_2_out, P3_out, plus_G2_out, plus_G3_out;

  and C_P0 (C_P0_out, P0, C);
  or plus_G0 (C1, G0, C_P0_out);
  and u_P1 (P1_out, C_P0_out, P1);
  and G0_P1 (G0_P1_out, G0, P1);
  or or_1 (or_1_out, P1_out, G0_P1_out);
  and G1_P2 (G1_P2_out, G1, P2);
  and u_P2 (P2_out, P1_out, P2);
  and P2_2 (P2_2_out, G0_P1_out, P2);
  or plus_G1 (C2, G1, or_1_out);
  or plus_G2 (plus_G2_out, G1_P2_out, G2);
  or or_2 (or_2_out, P2_out, P2_2_out);
  and G2_P3 (G2_P3_out, G2, P3);
  and u_P3 (P3_out, G1_P2_out, P3);
  and P3_2 (P3_2_out, P2_2_out, P3);
  and P0_P1 (P0_P1_out, P1, P0);
  and P2_P3 (P2_P3_out, P2, P3);
  or or_3 (C3, plus_G2_out, or_2_out);
  or plus_G3 (plus_G3_out, G3, G2_P3_out);
  or or_4 (or_4_out, P3_out, P3_2_out);
  and and_1 (GP, P0_P1_out, P2_P3_out);
  or or_5 (GG, plus_G3_out, or_4_out);
endmodule

module add_1bit (
  input  C,
  input  A,
  input  B,
  output S,
  output G,
  output P
);

  wire nand_1_out, nand_2_out, nand_3_out, nand_4_out, nand_5_out, nand_6_out, nand_7_out;

  nand nand_1 (nand_1_out, A, B);
  nand nand_2 (nand_2_out, A, nand_1_out);
  nand nand_3 (nand_3_out, nand_2_out, nand_4_out);
  nand nand_4 (nand_4_out, nand_1_out, B);
  not not_1 (G, nand_1_out);
  or or_1 (P, B, A);
  nand nand_5 (nand_5_out, C, nand_3_out);
  nand nand_6 (nand_6_out, C, nand_5_out);
  nand nand_7 (nand_7_out, nand_5_out, nand_3_out);
  nand nand_8 (S, nand_6_out, nand_7_out);
endmodule

module add_4bit (
  input  C,
  input  [3:0] A,
  input  [3:0] B,
  output [3:0] S,
  output G,
  output P
);

  wire add_1bit_1_g, add_1bit_1_p, add_1bit_2_g, add_1bit_2_p, add_1bit_3_g, add_1bit_3_p, add_1bit_4_g,
       add_1bit_4_p, carry_look_1_c1, carry_look_1_c2, carry_look_1_c3;

  add_1bit add_1bit_1 (.C(C), .A(A[0]), .B(B[0]), .S(S[0]), .G(add_1bit_1_g), .P(add_1bit_1_p));
  add_1bit add_1bit_2 (.C(carry_look_1_c1), .A(A[1]), .B(B[1]), .S(S[1]), .G(add_1bit_2_g), .P(add_1bit_2_p));
  add_1bit add_1bit_3 (.C(carry_look_1_c2), .A(A[2]), .B(B[2]), .S(S[2]), .G(add_1bit_3_g), .P(add_1bit_3_p));
  add_1bit add_1bit_4 (.C(carry_look_1_c3), .A(A[3]), .B(B[3]), .S(S[3]), .G(add_1bit_4_g), .P(add_1bit_4_p));
  carry_look carry_look_1 (
    .C(C), .G0(add_1bit_1_g), .P0(add_1bit_1_p), .G1(add_1bit_2_g), .P1(add_1bit_2_p), .G2(add_1bit_3_g),
    .P2(add_1bit_3_p), .G3(add_1bit_4_g), .P3(add_1bit_4_p), .C1(carry_look_1_c1), .C2(carry_look_1_c2),
    .C3(carry_look_1_c3), .GG(G), .GP(P));
endmodule

module add_16bit (
  input  C,
  input  [15:0] A,
  input  [15:0] B,
  output [15:0] S,
  output G,
  output P
);

  wire add_4bit_1_g, add_4bit_1_p, add_4bit_2_g, add_4bit_2_p, add_4bit_3_g, add_4bit_3_p, add_4bit_4_g,
       add_4bit_4_p, carry_look_1_c1, carry_look_1_c2, carry_look_1_c3;

  add_4bit add_4bit_1 (.C(C), .A(A[3:0]), .B(B[3:0]), .S(S[3:0]), .G(add_4bit_1_g), .P(add_4bit_1_p));
  add_4bit add_4bit_2 (.C(carry_look_1_c1), .A(A[7:4]), .B(B[7:4]), .S(S[7:4]), .G(add_4bit_2_g), .P(add_4bit_2_p));
  add_4bit add_4bit_3 (.C(carry_look_1_c2), .A(A[11:8]), .B(B[11:8]), .S(S[11:8]), .G(add_4bit_3_g), .P(add_4bit_3_p));
  add_4bit add_4bit_4 (
    .C(carry_look_1_c3), .A(A[15:12]), .B(B[15:12]), .S(S[15:12]), .G(add_4bit_4_g), .P(add_4bit_4_p));
  carry_look carry_look_1 (
    .C(C), .G0(add_4bit_1_g), .P0(add_4bit_1_p), .G1(add_4bit_2_g), .P1(add_4bit_2_p), .G2(add_4bit_3_g),
    .P2(add_4bit_3_p), .G3(add_4bit_4_g), .P3(add_4bit_4_p), .C1(carry_look_1_c1), .C2(carry_look_1_c2),
    .C3(carry_look_1_c3), .GG(G), .GP(P));
endmodule

module add_16bit_pc (
  input  [15:0] A,
  input  [15:0] B,
  output [15:0] S
);

  wire add_4bit_1_g, add_4bit_1_p, add_4bit_2_g, add_4bit_2_p, add_4bit_3_g, add_4bit_3_p, add_4bit_4_g,
       add_4bit_4_p, carry_look_1_c1, carry_look_1_c2, carry_look_1_c3;

  add_4bit add_4bit_1 (.C(1'b0), .A(A[3:0]), .B(B[3:0]), .S(S[3:0]), .G(add_4bit_1_g), .P(add_4bit_1_p));
  add_4bit add_4bit_2 (.C(carry_look_1_c1), .A(A[7:4]), .B(B[7:4]), .S(S[7:4]), .G(add_4bit_2_g), .P(add_4bit_2_p));
  add_4bit add_4bit_3 (.C(carry_look_1_c2), .A(A[11:8]), .B(B[11:8]), .S(S[11:8]), .G(add_4bit_3_g), .P(add_4bit_3_p));
  add_4bit add_4bit_4 (
    .C(carry_look_1_c3), .A(A[15:12]), .B(B[15:12]), .S(S[15:12]), .G(add_4bit_4_g), .P(add_4bit_4_p));
  carry_look carry_look_1 (
    .C(1'b0), .G0(add_4bit_1_g), .P0(add_4bit_1_p), .G1(add_4bit_2_g), .P1(add_4bit_2_p), .G2(add_4bit_3_g),
    .P2(add_4bit_3_p), .G3(add_4bit_4_g), .P3(add_4bit_4_p), .C1(carry_look_1_c1), .C2(carry_look_1_c2),
    .C3(carry_look_1_c3));  // open: GG, GP
endmodule

// +-SLT
module add_sub_16bit (
  input  SUB,
  input  Signed,
  input  [15:0] A,
  input  [15:0] B,
  output [15:0] S,
  output SLT
);

  wire A_B_out, add_16bit_1_g, add_16bit_1_p, and_1_out, nor_1_out, or_1_out, or_2_out, Sgn_2_out, Sgn_out,
       Usn_out, xor_2_out;
  wire [15:0] bit_extender_1_out, xor_1_out;

  assign bit_extender_1_out = {{15{SUB}}, SUB};  // Bit_Extender bit_extender_1
  assign xor_1_out = bit_extender_1_out ^ B;  // XOR_Gate xor_1, 16 bits wide
  nor nor_1 (nor_1_out, B[0], B[1], B[2], B[3], B[4], B[5], B[6], B[7], B[9], B[10], B[11], B[12], B[13], B[14], B[8], ~B[15]);  // NOR_Gate
  and A_B (A_B_out, A[15], xor_1_out[15]);
  nor Usn (Usn_out, Signed, or_1_out);
  add_16bit add_16bit_1 (.C(SUB), .A(A), .B(xor_1_out), .S(S), .G(add_16bit_1_g), .P(add_16bit_1_p));
  and and_1 (and_1_out, SUB, add_16bit_1_g);
  or or_1 (or_1_out, and_1_out, add_16bit_1_p);
  xor xor_2 (xor_2_out, nor_1_out, Signed);
  and Sgn (Sgn_out, A_B_out, Signed);
  and Sgn_2 (Sgn_2_out, S[15], xor_2_out);
  or or_2 (or_2_out, Sgn_2_out, Sgn_out, Usn_out);
  and u_SUB (SLT, or_2_out, SUB);
endmodule

module rightshift_16bit (
  input  [3:0] B,
  input  rotate,
  input  SRA,
  input  SLA,
  input  [15:0] A,
  output [15:0] S
);

  wire and_1_out, multiplexer_1_out, multiplexer_2_out, multiplexer_3_out, multiplexer_4_out,
       multiplexer_5_out, multiplexer_6_out, multiplexer_7_out, multiplexer_8_out, multiplexer_9_out,
       multiplexer_10_out, multiplexer_11_out, multiplexer_12_out, multiplexer_14_out, multiplexer_15_out,
       multiplexer_16_out, multiplexer_17_out, multiplexer_18_out, multiplexer_19_out, multiplexer_22_out,
       multiplexer_23_out, multiplexer_24_out, multiplexer_25_out, multiplexer_26_out, multiplexer_27_out,
       multiplexer_29_out, multiplexer_30_out, multiplexer_31_out, multiplexer_32_out, multiplexer_33_out,
       multiplexer_34_out, multiplexer_35_out, multiplexer_37_out, multiplexer_38_out, multiplexer_39_out,
       multiplexer_40_out, multiplexer_43_out, multiplexer_44_out, multiplexer_45_out, multiplexer_46_out,
       multiplexer_47_out, multiplexer_49_out, multiplexer_50_out, multiplexer_51_out, multiplexer_52_out,
       multiplexer_53_out, multiplexer_55_out, multiplexer_56_out, multiplexer_57_out, multiplexer_60_out,
       multiplexer_61_out, multiplexer_62_out, multiplexer_63_out, multiplexer_65_out, multiplexer_66_out,
       multiplexer_67_out, multiplexer_68_out, multiplexer_69_out, multiplexer_71_out, multiplexer_72_out,
       multiplexer_73_out, multiplexer_76_out, multiplexer_77_out, multiplexer_78_out, multiplexer_79_out;

  and and_1 (and_1_out, SRA, A[15]);
  Multiplexer #(.enable("false")) multiplexer_1 (
    .in0(A[15]), .in1(multiplexer_3_out), .out(multiplexer_1_out), .sel(B[3]));
  Multiplexer #(.enable("false")) multiplexer_2 (.in0(and_1_out), .in1(A[6]), .out(multiplexer_2_out), .sel(rotate));
  Multiplexer #(.enable("false")) multiplexer_3 (.in0(and_1_out), .in1(A[7]), .out(multiplexer_3_out), .sel(rotate));
  Multiplexer #(.enable("false")) multiplexer_4 (
    .in0(A[14]), .in1(multiplexer_2_out), .out(multiplexer_4_out), .sel(B[3]));
  Multiplexer #(.enable("false")) multiplexer_5 (
    .in0(and_1_out), .in1(multiplexer_60_out), .out(multiplexer_5_out), .sel(rotate));
  Multiplexer #(.enable("false")) multiplexer_6 (
    .in0(and_1_out), .in1(multiplexer_65_out), .out(multiplexer_6_out), .sel(rotate));
  Multiplexer #(.enable("false")) multiplexer_7 (
    .in0(multiplexer_1_out), .in1(multiplexer_5_out), .out(multiplexer_7_out), .sel(B[2]));
  Multiplexer #(.enable("false")) multiplexer_8 (
    .in0(multiplexer_4_out), .in1(multiplexer_6_out), .out(multiplexer_8_out), .sel(B[2]));
  Multiplexer #(.enable("false")) multiplexer_9 (
    .in0(and_1_out), .in1(multiplexer_72_out), .out(multiplexer_9_out), .sel(rotate));
  Multiplexer #(.enable("false")) multiplexer_10 (
    .in0(multiplexer_8_out), .in1(multiplexer_18_out), .out(multiplexer_10_out), .sel(B[1]));
  Multiplexer #(.enable("false")) multiplexer_11 (
    .in0(multiplexer_7_out), .in1(multiplexer_9_out), .out(multiplexer_11_out), .sel(B[1]));
  Multiplexer #(.enable("false")) multiplexer_12 (
    .in0(and_1_out), .in1(multiplexer_78_out), .out(multiplexer_12_out), .sel(rotate));
  Multiplexer #(.enable("false")) multiplexer_13 (
    .in0(multiplexer_11_out), .in1(multiplexer_12_out), .out(S[15]), .sel(B[0]));
  Multiplexer #(.enable("false")) multiplexer_14 (.in0(and_1_out), .in1(A[5]), .out(multiplexer_14_out), .sel(rotate));
  Multiplexer #(.enable("false")) multiplexer_15 (
    .in0(A[13]), .in1(multiplexer_14_out), .out(multiplexer_15_out), .sel(B[3]));
  Multiplexer #(.enable("false")) multiplexer_16 (
    .in0(and_1_out), .in1(multiplexer_71_out), .out(multiplexer_16_out), .sel(rotate));
  Multiplexer #(.enable("false")) multiplexer_17 (
    .in0(multiplexer_15_out), .in1(multiplexer_16_out), .out(multiplexer_17_out), .sel(B[2]));
  Multiplexer #(.enable("false")) multiplexer_18 (
    .in0(and_1_out), .in1(multiplexer_77_out), .out(multiplexer_18_out), .sel(rotate));
  Multiplexer #(.enable("false")) multiplexer_19 (
    .in0(multiplexer_17_out), .in1(multiplexer_7_out), .out(multiplexer_19_out), .sel(B[1]));
  Multiplexer #(.enable("false")) multiplexer_20 (
    .in0(multiplexer_19_out), .in1(multiplexer_10_out), .out(S[13]), .sel(B[0]));
  Multiplexer #(.enable("false")) multiplexer_21 (
    .in0(multiplexer_10_out), .in1(multiplexer_11_out), .out(S[14]), .sel(B[0]));
  Multiplexer #(.enable("false")) multiplexer_22 (.in0(and_1_out), .in1(A[4]), .out(multiplexer_22_out), .sel(rotate));
  Multiplexer #(.enable("false")) multiplexer_23 (
    .in0(A[11]), .in1(multiplexer_30_out), .out(multiplexer_23_out), .sel(B[3]));
  Multiplexer #(.enable("false")) multiplexer_24 (
    .in0(A[12]), .in1(multiplexer_22_out), .out(multiplexer_24_out), .sel(B[3]));
  Multiplexer #(.enable("false")) multiplexer_25 (
    .in0(and_1_out), .in1(multiplexer_76_out), .out(multiplexer_25_out), .sel(rotate));
  Multiplexer #(.enable("false")) multiplexer_26 (
    .in0(multiplexer_24_out), .in1(multiplexer_25_out), .out(multiplexer_26_out), .sel(B[2]));
  Multiplexer #(.enable("false")) multiplexer_27 (
    .in0(multiplexer_26_out), .in1(multiplexer_8_out), .out(multiplexer_27_out), .sel(B[1]));
  Multiplexer #(.enable("false")) multiplexer_28 (
    .in0(multiplexer_27_out), .in1(multiplexer_19_out), .out(S[12]), .sel(B[0]));
  Multiplexer #(.enable("false")) multiplexer_29 (.in0(and_1_out), .in1(A[2]), .out(multiplexer_29_out), .sel(rotate));
  Multiplexer #(.enable("false")) multiplexer_30 (.in0(and_1_out), .in1(A[3]), .out(multiplexer_30_out), .sel(rotate));
  Multiplexer #(.enable("false")) multiplexer_31 (
    .in0(A[10]), .in1(multiplexer_29_out), .out(multiplexer_31_out), .sel(B[3]));
  Multiplexer #(.enable("false")) multiplexer_32 (
    .in0(multiplexer_31_out), .in1(multiplexer_4_out), .out(multiplexer_32_out), .sel(B[2]));
  Multiplexer #(.enable("false")) multiplexer_33 (
    .in0(multiplexer_23_out), .in1(multiplexer_1_out), .out(multiplexer_33_out), .sel(B[2]));
  Multiplexer #(.enable("false")) multiplexer_34 (
    .in0(multiplexer_33_out), .in1(multiplexer_17_out), .out(multiplexer_34_out), .sel(B[1]));
  Multiplexer #(.enable("false")) multiplexer_35 (
    .in0(multiplexer_32_out), .in1(multiplexer_26_out), .out(multiplexer_35_out), .sel(B[1]));
  Multiplexer #(.enable("false")) multiplexer_36 (
    .in0(multiplexer_34_out), .in1(multiplexer_27_out), .out(S[11]), .sel(B[0]));
  Multiplexer #(.enable("false")) multiplexer_37 (.in0(and_1_out), .in1(A[1]), .out(multiplexer_37_out), .sel(rotate));
  Multiplexer #(.enable("false")) multiplexer_38 (
    .in0(A[9]), .in1(multiplexer_37_out), .out(multiplexer_38_out), .sel(B[3]));
  Multiplexer #(.enable("false")) multiplexer_39 (
    .in0(multiplexer_38_out), .in1(multiplexer_15_out), .out(multiplexer_39_out), .sel(B[2]));
  Multiplexer #(.enable("false")) multiplexer_40 (
    .in0(multiplexer_39_out), .in1(multiplexer_33_out), .out(multiplexer_40_out), .sel(B[1]));
  Multiplexer #(.enable("false")) multiplexer_41 (
    .in0(multiplexer_35_out), .in1(multiplexer_34_out), .out(S[10]), .sel(B[0]));
  Multiplexer #(.enable("false")) multiplexer_42 (
    .in0(multiplexer_40_out), .in1(multiplexer_35_out), .out(S[9]), .sel(B[0]));
  Multiplexer #(.enable("false")) multiplexer_43 (.in0(and_1_out), .in1(A[0]), .out(multiplexer_43_out), .sel(rotate));
  Multiplexer #(.enable("false")) multiplexer_44 (
    .in0(A[8]), .in1(multiplexer_43_out), .out(multiplexer_44_out), .sel(B[3]));
  Multiplexer #(.enable("false")) multiplexer_45 (.in0(A[7]), .in1(A[15]), .out(multiplexer_45_out), .sel(B[3]));
  Multiplexer #(.enable("false")) multiplexer_46 (
    .in0(multiplexer_44_out), .in1(multiplexer_24_out), .out(multiplexer_46_out), .sel(B[2]));
  Multiplexer #(.enable("false")) multiplexer_47 (
    .in0(multiplexer_46_out), .in1(multiplexer_32_out), .out(multiplexer_47_out), .sel(B[1]));
  Multiplexer #(.enable("false")) multiplexer_48 (
    .in0(multiplexer_47_out), .in1(multiplexer_40_out), .out(S[8]), .sel(B[0]));
  Multiplexer #(.enable("false")) multiplexer_49 (.in0(A[6]), .in1(A[14]), .out(multiplexer_49_out), .sel(B[3]));
  Multiplexer #(.enable("false")) multiplexer_50 (
    .in0(multiplexer_45_out), .in1(multiplexer_23_out), .out(multiplexer_50_out), .sel(B[2]));
  Multiplexer #(.enable("false")) multiplexer_51 (
    .in0(multiplexer_49_out), .in1(multiplexer_31_out), .out(multiplexer_51_out), .sel(B[2]));
  Multiplexer #(.enable("false")) multiplexer_52 (
    .in0(multiplexer_50_out), .in1(multiplexer_39_out), .out(multiplexer_52_out), .sel(B[1]));
  Multiplexer #(.enable("false")) multiplexer_53 (
    .in0(multiplexer_51_out), .in1(multiplexer_46_out), .out(multiplexer_53_out), .sel(B[1]));
  Multiplexer #(.enable("false")) multiplexer_54 (
    .in0(multiplexer_52_out), .in1(multiplexer_47_out), .out(S[7]), .sel(B[0]));
  Multiplexer #(.enable("false")) multiplexer_55 (.in0(A[5]), .in1(A[13]), .out(multiplexer_55_out), .sel(B[3]));
  Multiplexer #(.enable("false")) multiplexer_56 (
    .in0(multiplexer_55_out), .in1(multiplexer_38_out), .out(multiplexer_56_out), .sel(B[2]));
  Multiplexer #(.enable("false")) multiplexer_57 (
    .in0(multiplexer_56_out), .in1(multiplexer_50_out), .out(multiplexer_57_out), .sel(B[1]));
  Multiplexer #(.enable("false")) multiplexer_58 (
    .in0(multiplexer_57_out), .in1(multiplexer_53_out), .out(S[5]), .sel(B[0]));
  Multiplexer #(.enable("false")) multiplexer_59 (
    .in0(multiplexer_53_out), .in1(multiplexer_52_out), .out(S[6]), .sel(B[0]));
  Multiplexer #(.enable("false")) multiplexer_60 (.in0(A[3]), .in1(A[11]), .out(multiplexer_60_out), .sel(B[3]));
  Multiplexer #(.enable("false")) multiplexer_61 (.in0(A[4]), .in1(A[12]), .out(multiplexer_61_out), .sel(B[3]));
  Multiplexer #(.enable("false")) multiplexer_62 (
    .in0(multiplexer_61_out), .in1(multiplexer_44_out), .out(multiplexer_62_out), .sel(B[2]));
  Multiplexer #(.enable("false")) multiplexer_63 (
    .in0(multiplexer_62_out), .in1(multiplexer_51_out), .out(multiplexer_63_out), .sel(B[1]));
  Multiplexer #(.enable("false")) multiplexer_64 (
    .in0(multiplexer_63_out), .in1(multiplexer_57_out), .out(S[4]), .sel(B[0]));
  Multiplexer #(.enable("false")) multiplexer_65 (.in0(A[2]), .in1(A[10]), .out(multiplexer_65_out), .sel(B[3]));
  Multiplexer #(.enable("false")) multiplexer_66 (
    .in0(multiplexer_65_out), .in1(multiplexer_49_out), .out(multiplexer_66_out), .sel(B[2]));
  Multiplexer #(.enable("false")) multiplexer_67 (
    .in0(multiplexer_60_out), .in1(multiplexer_45_out), .out(multiplexer_67_out), .sel(B[2]));
  Multiplexer #(.enable("false")) multiplexer_68 (
    .in0(multiplexer_67_out), .in1(multiplexer_56_out), .out(multiplexer_68_out), .sel(B[1]));
  Multiplexer #(.enable("false")) multiplexer_69 (
    .in0(multiplexer_66_out), .in1(multiplexer_62_out), .out(multiplexer_69_out), .sel(B[1]));
  Multiplexer #(.enable("false")) multiplexer_70 (
    .in0(multiplexer_68_out), .in1(multiplexer_63_out), .out(S[3]), .sel(B[0]));
  Multiplexer #(.enable("false")) multiplexer_71 (.in0(A[1]), .in1(A[9]), .out(multiplexer_71_out), .sel(B[3]));
  Multiplexer #(.enable("false")) multiplexer_72 (
    .in0(multiplexer_71_out), .in1(multiplexer_55_out), .out(multiplexer_72_out), .sel(B[2]));
  Multiplexer #(.enable("false")) multiplexer_73 (
    .in0(multiplexer_72_out), .in1(multiplexer_67_out), .out(multiplexer_73_out), .sel(B[1]));
  Multiplexer #(.enable("false")) multiplexer_74 (
    .in0(multiplexer_73_out), .in1(multiplexer_69_out), .out(S[1]), .sel(B[0]));
  Multiplexer #(.enable("false")) multiplexer_75 (
    .in0(multiplexer_69_out), .in1(multiplexer_68_out), .out(S[2]), .sel(B[0]));
  Multiplexer #(.enable("false")) multiplexer_76 (.in0(A[0]), .in1(A[8]), .out(multiplexer_76_out), .sel(B[3]));
  Multiplexer #(.enable("false")) multiplexer_77 (
    .in0(multiplexer_76_out), .in1(multiplexer_61_out), .out(multiplexer_77_out), .sel(B[2]));
  Multiplexer #(.enable("false")) multiplexer_78 (
    .in0(multiplexer_77_out), .in1(multiplexer_66_out), .out(multiplexer_78_out), .sel(B[1]));
  Multiplexer #(.enable("false")) multiplexer_79 (
    .in0(multiplexer_78_out), .in1(multiplexer_73_out), .out(multiplexer_79_out), .sel(B[0]));
  Multiplexer #(.enable("false")) multiplexer_80 (.in0(multiplexer_79_out), .in1(A[0]), .out(S[0]), .sel(SLA));
endmodule

module reverse_16bit (
  input  [15:0] A,
  input  Flip,
  output [15:0] S
);

  Multiplexer #(.enable("false")) multiplexer_1 (.in0(A[15]), .in1(A[0]), .out(S[15]), .sel(Flip));
  Multiplexer #(.enable("false")) multiplexer_2 (.in0(A[14]), .in1(A[1]), .out(S[14]), .sel(Flip));
  Multiplexer #(.enable("false")) multiplexer_3 (.in0(A[13]), .in1(A[2]), .out(S[13]), .sel(Flip));
  Multiplexer #(.enable("false")) multiplexer_4 (.in0(A[12]), .in1(A[3]), .out(S[12]), .sel(Flip));
  Multiplexer #(.enable("false")) multiplexer_5 (.in0(A[11]), .in1(A[4]), .out(S[11]), .sel(Flip));
  Multiplexer #(.enable("false")) multiplexer_6 (.in0(A[9]), .in1(A[6]), .out(S[9]), .sel(Flip));
  Multiplexer #(.enable("false")) multiplexer_7 (.in0(A[10]), .in1(A[5]), .out(S[10]), .sel(Flip));
  Multiplexer #(.enable("false")) multiplexer_8 (.in0(A[8]), .in1(A[7]), .out(S[8]), .sel(Flip));
  Multiplexer #(.enable("false")) multiplexer_9 (.in0(A[7]), .in1(A[8]), .out(S[7]), .sel(Flip));
  Multiplexer #(.enable("false")) multiplexer_10 (.in0(A[6]), .in1(A[9]), .out(S[6]), .sel(Flip));
  Multiplexer #(.enable("false")) multiplexer_11 (.in0(A[5]), .in1(A[10]), .out(S[5]), .sel(Flip));
  Multiplexer #(.enable("false")) multiplexer_12 (.in0(A[3]), .in1(A[12]), .out(S[3]), .sel(Flip));
  Multiplexer #(.enable("false")) multiplexer_13 (.in0(A[4]), .in1(A[11]), .out(S[4]), .sel(Flip));
  Multiplexer #(.enable("false")) multiplexer_14 (.in0(A[1]), .in1(A[14]), .out(S[1]), .sel(Flip));
  Multiplexer #(.enable("false")) multiplexer_15 (.in0(A[2]), .in1(A[13]), .out(S[2]), .sel(Flip));
  Multiplexer #(.enable("false")) multiplexer_16 (.in0(A[0]), .in1(A[15]), .out(S[0]), .sel(Flip));
endmodule

// SLRA
module shift_16bit (
  input  [3:0] B,
  input  [15:0] A,
  input  Left,
  input  Arithmetic,
  input  Rotate,
  output [15:0] S
);

  wire [15:0] reverse_16bit_1_s, rightshift_16bit_1_s;

  reverse_16bit reverse_16bit_1 (.Flip(Left), .A(A), .S(reverse_16bit_1_s));
  rightshift_16bit rightshift_16bit_1 (
    .SLA(Arithmetic), .B(B), .rotate(Rotate), .SRA(Arithmetic), .A(reverse_16bit_1_s),
    .S(rightshift_16bit_1_s));
  reverse_16bit reverse_16bit_2 (.Flip(Left), .A(rightshift_16bit_1_s), .S(S));
endmodule

// PC
module PC_pipelined (
  input  clk,
  input  reset,
  input  update,
  input  branch,
  input  [15:0] branch_pc,
  output [15:0] pc,
  output [15:0] next_pc
);

  wire or_1_out;
  wire [15:0] multiplexer_1_out, multiplexer_2_out;

  Multiplexer #(.width(16), .disabled(0), .enable("false")) multiplexer_1 (
    .in0(next_pc), .in1(branch_pc), .out(multiplexer_1_out), .sel(branch));
  or or_1 (or_1_out, reset, update);
  Multiplexer #(.width(16), .disabled(0), .enable("false")) multiplexer_2 (
    .in0(multiplexer_1_out), .in1({16{1'b0}}), .out(multiplexer_2_out), .sel(reset));
  Register #(.width(16)) register_1 (.D(multiplexer_2_out), .en(or_1_out), .Q(pc), .clk(clk));  // open: clr
  add_16bit_pc add_16bit_pc_1 (.A(pc), .B(16'h2), .S(next_pc));
endmodule

// DePC
module PC_decode (
  input  clk,
  input  reset,
  input  [15:0] pc,
  input  [15:0] next_pc,
  output [15:0] decode_pc,
  output [15:0] decode_next_pc
);

  Register #(.width(16)) register_1 (.D(pc), .Q(decode_pc), .clk(clk), .clr(reset));  // open: en
  Register #(.width(16)) register_2 (.D(next_pc), .Q(decode_next_pc), .clk(clk), .clr(reset));  // open: en
endmodule

module decode_op (
  input  [4:0] opcode,
  output LUI,
  output AUIPC,
  output U,
  output J,
  output B,
  output LD,
  output Imm,
  output JALR,
  output I,
  output S,
  output halt,
  output R,
  output [2:0] alu_op
);

  wire alu_op_out, jmp_out, S_out, SB_out, SH_out;
  wire [2:0] multiplexer_1_out, multiplexer_2_out;

  nor nor_1 (halt, opcode[0], opcode[1], opcode[2], opcode[3], opcode[4]);
  and jmp (jmp_out, ~opcode[4], opcode[3], ~opcode[2], opcode[1]);  // AND_Gate
  and u_S (S_out, opcode[0], ~opcode[3], ~opcode[4]);  // AND_Gate
  and SH (SH_out, opcode[2], opcode[1], S_out);
  or S_2 (S, SH_out, SB_out);
  and SB (SB_out, S_out, ~opcode[1], ~opcode[2]);  // AND_Gate
  Multiplexer #(.width(3), .enable("false")) multiplexer_1 (
    .in0(3'b000), .in1(3'b001), .out(multiplexer_1_out), .sel(SH_out));
  and u_U (U, ~opcode[4], ~opcode[3], ~opcode[2], opcode[1]);  // AND_Gate
  and u_J (J, ~opcode[0], jmp_out);  // AND_Gate
  and u_B (B, ~jmp_out, ~opcode[4], opcode[3]);  // AND_Gate
  and u_LD (LD, ~opcode[4], ~opcode[3], opcode[2], ~S);  // AND_Gate
  and u_Imm (Imm, opcode[4], opcode[3]);
  and u_JALR (JALR, jmp_out, opcode[0]);
  and u_R (R, opcode[4], ~opcode[3]);  // AND_Gate
  and u_LUI (LUI, ~opcode[0], U);  // AND_Gate
  and u_AUIPC (AUIPC, U, opcode[0]);
  Multiplexer #(.width(3), .enable("false")) multiplexer_2 (
    .in0(multiplexer_1_out), .in1({opcode[1], 1'b0, opcode[0]}), .out(multiplexer_2_out), .sel(LD));
  or u_alu_op (alu_op_out, B, Imm, R);
  Multiplexer #(.width(3), .enable("false")) multiplexer_3 (
    .in0(multiplexer_2_out), .in1(opcode[2:0]), .out(alu_op), .sel(alu_op_out));
  or u_I (I, LD, Imm, JALR);
endmodule

// ID
module Instruction_Decode (
  input  [15:0] Instruction,
  output [15:0] Immediate,
  output alu_imm,
  output pc_2_alu,
  output pc_from_alu,
  output reg_wr,
  output [2:0] rd,
  output [2:0] rs1,
  output [2:0] rs2,
  output pc_rd,
  output b_unc,
  output halt,
  output b_nz,
  output b_z,
  output alu_op_alt,
  output [2:0] alu_op,
  output mem_rd,
  output mem_wr,
  output [2:0] read_op
);

  wire alu_imm_out, bc_out, decode_op_1_auipc, decode_op_1_b, decode_op_1_i, decode_op_1_imm, decode_op_1_j,
       decode_op_1_jalr, decode_op_1_ld, decode_op_1_lui, decode_op_1_r, decode_op_1_s, decode_op_1_u,
       imm_op_alt_out, nor_1_out, not_1_out, or_1_out, R_op_alt_out, reg_wr_out;
  wire [2:0] multiplexer_5_out;
  wire [15:0] multiplexer_1_out, multiplexer_2_out, multiplexer_3_out, multiplexer_4_out;

  decode_op decode_op_1 (
    .halt(halt), .opcode(Instruction[4:0]), .LUI(decode_op_1_lui), .AUIPC(decode_op_1_auipc),
    .U(decode_op_1_u), .J(decode_op_1_j), .B(decode_op_1_b), .LD(decode_op_1_ld), .Imm(decode_op_1_imm),
    .JALR(decode_op_1_jalr), .I(decode_op_1_i), .S(decode_op_1_s), .R(decode_op_1_r), .alu_op(read_op));
  not not_1 (not_1_out, decode_op_1_lui);
  assign rs1 = not_1_out ? Instruction[10:8] : 3'bz;  // Controlled_Buffer controlled_buffer_1
  xor bc (bc_out, read_op[0], read_op[2]);
  and R_op_alt (R_op_alt_out, Instruction[15], decode_op_1_r);
  Pull_Resistor pull_resistor_1 (.node(rs1));
  nor nor_1 (nor_1_out, decode_op_1_ld, decode_op_1_s, decode_op_1_u);
  Multiplexer #(.width(16), .enable("false")) multiplexer_1 (
    .in0({16{1'b0}}), .in1({Instruction[15:8], {8{1'b0}}}), .out(multiplexer_1_out), .sel(decode_op_1_u));
  Multiplexer #(.width(16), .enable("false")) multiplexer_2 (
    .in0({16{1'b0}}), .in1({{8{Instruction[15]}}, Instruction[14:8], 1'b0}), .out(multiplexer_2_out),
    .sel(decode_op_1_j));
  or or_1 (or_1_out, decode_op_1_s, decode_op_1_b);
  and imm_op_alt (imm_op_alt_out, decode_op_1_imm, read_op[0], ~read_op[1], read_op[2], Instruction[15]);  // AND_Gate
  or ub (b_unc, decode_op_1_jalr, decode_op_1_j);
  buf pc2alu (pc_2_alu, decode_op_1_auipc);
  buf pc_f_alu (pc_from_alu, decode_op_1_jalr);
  nor u_reg_wr (reg_wr_out, decode_op_1_s, decode_op_1_b);
  nor u_alu_imm (alu_imm_out, decode_op_1_b, decode_op_1_r, decode_op_1_j);
  Multiplexer #(.width(16), .enable("false")) multiplexer_3 (
    .in0({16{1'b0}}), .in1({{11{Instruction[15]}}, Instruction[14], Instruction[7:5], 1'b0}),
    .out(multiplexer_3_out), .sel(or_1_out));
  Multiplexer #(.width(16), .enable("false")) multiplexer_4 (
    .in0({16{1'b0}}), .in1({{12{Instruction[15]}}, Instruction[14:11]}), .out(multiplexer_4_out),
    .sel(decode_op_1_i));
  and and_1 (reg_wr, reg_wr_out, ~halt);  // AND_Gate
  and and_2 (alu_imm, alu_imm_out, ~halt);  // AND_Gate
  assign Immediate = multiplexer_1_out | multiplexer_2_out | multiplexer_3_out | multiplexer_4_out;  // OR_Gate or_2, 16 bits wide
  and bnz (b_nz, bc_out, decode_op_1_b);
  and bz (b_z, decode_op_1_b, ~bc_out);  // AND_Gate
  Multiplexer #(.width(3), .enable("false")) multiplexer_5 (
    .in0(3'b000), .in1(read_op), .out(multiplexer_5_out), .sel(nor_1_out));
  buf u_mem_rd (mem_rd, decode_op_1_ld);
  buf u_mem_wr (mem_wr, decode_op_1_s);
  or op_alt (alu_op_alt, decode_op_1_b, imm_op_alt_out, R_op_alt_out);
  Multiplexer #(.width(3), .enable("false")) multiplexer_6 (
    .in0(multiplexer_5_out), .in1({1'b0, read_op[2:1]}), .out(alu_op), .sel(decode_op_1_b));

  assign pc_rd = b_unc;
  assign rd = Instruction[7:5];
  assign rs2 = Instruction[13:11];

  // Notes on the sheet:
  //   U-type
  //   J-type
  //   S&B-type
  //   I-type
endmodule

// &^|
module AND_X_OR (
  input  [1:0] Sel,
  input  [15:0] A,
  input  [15:0] B,
  output [15:0] S
);

  wire [15:0] bit_extender_1_out, bit_extender_2_out, nand_1_out, nand_2_out, nand_3_out, nand_4_out,
       nand_5_out, nand_6_out;

  assign nand_1_out = ~(A & B);  // NAND_Gate nand_1, 16 bits wide
  assign bit_extender_1_out = {{15{Sel[1]}}, Sel[1]};  // Bit_Extender bit_extender_1
  assign bit_extender_2_out = {{15{Sel[0]}}, Sel[0]};  // Bit_Extender bit_extender_2
  assign nand_2_out = ~(A & nand_1_out);  // NAND_Gate nand_2, 16 bits wide
  assign nand_3_out = ~(nand_1_out & B);  // NAND_Gate nand_3, 16 bits wide
  assign nand_4_out = ~(~nand_1_out & bit_extender_1_out);  // NAND_Gate nand_4, 16 bits wide
  assign nand_5_out = ~(nand_2_out & nand_3_out);  // NAND_Gate nand_5, 16 bits wide
  assign nand_6_out = ~(nand_5_out & ~bit_extender_2_out);  // NAND_Gate nand_6, 16 bits wide
  assign S = ~(nand_6_out & nand_4_out);  // NAND_Gate nand_7, 16 bits wide
endmodule

// ALU
module ALU_pipelined (
  input  clk,
  input  reset,
  input  op_alt,
  input  [2:0] op,
  input  [15:0] A,
  input  [15:0] B,
  output [15:0] ALU_out,
  output Zero
);

  wire add_sub_16bit_1_slt, and_1_out, and_2_out, and_3_out, decoder_1_out0, decoder_1_out1, decoder_1_out2,
       decoder_1_out3, nor_1_out, not_1_out, or_1_out, or_2_out, or_3_out, or_4_out, SRA_out;
  wire [15:0] add_sub_16bit_1_s, and_x_or_1_s, bit_extender_1_out, multiplexer_1_out, multiplexer_2_out,
       multiplexer_3_out, shift_16bit_1_s;

  Decoder #(.select(2), .enable("false")) decoder_1 (
    .out0(decoder_1_out0), .out1(decoder_1_out1), .out2(decoder_1_out2), .out3(decoder_1_out3), .sel(op[1:0]));
  AND_X_OR and_x_or_1 (.Sel(op[1:0]), .A(A), .B(B), .S(and_x_or_1_s));
  and and_1 (and_1_out, ~op[2], decoder_1_out1);  // AND_Gate
  and SRA (SRA_out, op_alt, op[2]);
  or or_1 (or_1_out, decoder_1_out2, decoder_1_out3);
  and and_2 (and_2_out, decoder_1_out0, op_alt);
  or or_2 (or_2_out, and_2_out, or_1_out);
  add_sub_16bit add_sub_16bit_1 (
    .SUB(or_2_out), .Signed(decoder_1_out2), .A(A), .B(B), .S(add_sub_16bit_1_s), .SLT(add_sub_16bit_1_slt));
  shift_16bit shift_16bit_1 (
    .Left(and_1_out), .Arithmetic(SRA_out), .Rotate(1'b0), .B(B[3:0]), .A(A), .S(shift_16bit_1_s));
  assign bit_extender_1_out = {{15{add_sub_16bit_1_slt}}, add_sub_16bit_1_slt};  // Bit_Extender bit_extender_1
  or or_3 (or_3_out, or_1_out, ~decoder_1_out0);  // OR_Gate
  not not_1 (not_1_out, or_1_out);
  Multiplexer #(.width(16), .disabled(0), .enable("false")) multiplexer_1 (
    .in0(add_sub_16bit_1_s), .in1(multiplexer_2_out), .out(multiplexer_1_out), .sel(or_3_out));
  Multiplexer #(.width(16), .disabled(0), .enable("false")) multiplexer_2 (
    .in0(bit_extender_1_out), .in1(shift_16bit_1_s), .out(multiplexer_2_out), .sel(not_1_out));
  and and_3 (and_3_out, op[2], decoder_1_out1);
  or or_4 (or_4_out, ~op[2], and_3_out);  // OR_Gate
  Multiplexer #(.width(16), .disabled(0), .enable("false")) multiplexer_3 (
    .in0(and_x_or_1_s), .in1(multiplexer_1_out), .out(multiplexer_3_out), .sel(or_4_out));
  nor nor_1 (nor_1_out, multiplexer_3_out[0], multiplexer_3_out[1], multiplexer_3_out[2], multiplexer_3_out[3], multiplexer_3_out[4], multiplexer_3_out[5], multiplexer_3_out[6], multiplexer_3_out[7], multiplexer_3_out[9], multiplexer_3_out[10], multiplexer_3_out[11], multiplexer_3_out[12], multiplexer_3_out[13], multiplexer_3_out[14], multiplexer_3_out[15], multiplexer_3_out[8]);
  Register #(.width(16)) register_1 (.D(multiplexer_3_out), .Q(ALU_out), .clk(clk), .clr(reset));  // open: en
  Register #(.width(1)) register_2 (.D(nor_1_out), .Q(Zero), .clk(clk), .clr(reset));  // open: en
endmodule

module rs_rd_rs__0 (
  input  [2:0] rs,
  input  [2:0] rd,
  output mem_cond
);

  wire or_1_out;
  wire [2:0] xnor_1_out;

  or or_1 (or_1_out, rs[2], rs[1], rs[0]);
  and and_1 (mem_cond, or_1_out, xnor_1_out[2], xnor_1_out[1], xnor_1_out[0]);
  assign xnor_1_out = ~(rs ^ rd);  // XNOR_Gate xnor_1, 3 bits wide
endmodule

// REG
module Registers_pipelined (
  input  reg_wr,
  input  clk,
  input  reset,
  input  [2:0] rd_a,
  input  [2:0] r1_a,
  input  [2:0] r2_a,
  input  [15:0] wr,
  output [15:0] r1_d,
  output [15:0] r2_d
);

  wire decoder_1_out1, decoder_1_out2, decoder_1_out3, decoder_1_out4, decoder_1_out5, decoder_1_out6,
       decoder_1_out7, rs_rd_rs_0_1_mem_cond, rs_rd_rs_0_2_mem_cond;
  wire [2:0] multiplexer_1_out, multiplexer_3_out, register_1_q, register_2_q;
  wire [15:0] register_3_q, register_4_q, register_5_q, register_6_q, register_7_q, register_8_q,
       register_9_q;

  Register #(.width(3)) register_1 (.D(r1_a), .Q(register_1_q), .clk(clk), .clr(reset));  // open: en
  Register #(.width(3)) register_2 (.D(r2_a), .Q(register_2_q), .clk(clk), .clr(reset));  // open: en
  Decoder #(.select(3), .disabled(0)) decoder_1 (
    .out1(decoder_1_out1), .out2(decoder_1_out2), .out3(decoder_1_out3), .out4(decoder_1_out4),
    .out5(decoder_1_out5), .out6(decoder_1_out6), .out7(decoder_1_out7), .sel(rd_a), .en(reg_wr));  // open: out0
  Register #(.width(16)) register_3 (.D(wr), .en(decoder_1_out1), .Q(register_3_q), .clk(clk), .clr(reset));
  Register #(.width(16)) register_4 (.D(wr), .en(decoder_1_out2), .Q(register_4_q), .clk(clk), .clr(reset));
  Register #(.width(16)) register_5 (.D(wr), .en(decoder_1_out3), .Q(register_5_q), .clk(clk), .clr(reset));
  Register #(.width(16)) register_6 (.D(wr), .en(decoder_1_out4), .Q(register_6_q), .clk(clk), .clr(reset));
  Register #(.width(16)) register_7 (.D(wr), .en(decoder_1_out5), .Q(register_7_q), .clk(clk), .clr(reset));
  Register #(.width(16)) register_8 (.D(wr), .en(decoder_1_out6), .Q(register_8_q), .clk(clk), .clr(reset));
  Register #(.width(16)) register_9 (.D(wr), .en(decoder_1_out7), .Q(register_9_q), .clk(clk), .clr(reset));
  rs_rd_rs__0 rs_rd_rs_0_1 (.mem_cond(rs_rd_rs_0_1_mem_cond), .rs(register_1_q), .rd(rd_a));
  Multiplexer #(.width(3), .enable("false")) multiplexer_1 (
    .in0(register_1_q), .in1(rd_a), .out(multiplexer_1_out), .sel(rs_rd_rs_0_1_mem_cond));
  Multiplexer #(.select(3), .width(16), .enable("false")) multiplexer_2 (
    .in0({16{1'b0}}), .in1(register_3_q), .in2(register_4_q), .in3(register_5_q), .in4(register_6_q),
    .in5(register_7_q), .in6(register_8_q), .in7(register_9_q), .out(r1_d), .sel(multiplexer_1_out));
  rs_rd_rs__0 rs_rd_rs_0_2 (.mem_cond(rs_rd_rs_0_2_mem_cond), .rs(register_2_q), .rd(rd_a));
  Multiplexer #(.width(3), .enable("false")) multiplexer_3 (
    .in0(register_2_q), .in1(rd_a), .out(multiplexer_3_out), .sel(rs_rd_rs_0_2_mem_cond));
  Multiplexer #(.select(3), .width(16), .enable("false")) multiplexer_4 (
    .in0({16{1'b0}}), .in1(register_3_q), .in2(register_4_q), .in3(register_5_q), .in4(register_6_q),
    .in5(register_7_q), .in6(register_8_q), .in7(register_9_q), .out(r2_d), .sel(multiplexer_3_out));

  // Notes on the sheet:
  //   ra
  //   sp
  //   gp
  //   tp
  //   t0
  //   t1
  //   t2
endmodule

// EX_in
module Ex_Input (
  input  branch,
  input  rd_mem_thn_reg_nxt,
  input  reset,
  input  clk,
  input  [15:0] decode_pc,
  input  [15:0] decode_next_pc,
  input  [15:0] Immediate,
  input  alu_imm,
  input  pc_2_alu,
  input  pc_from_alu,
  input  reg_wr,
  input  [2:0] rd,
  input  [2:0] rs1,
  input  [2:0] rs2,
  input  pc_rd,
  input  b_unc,
  input  b_nz,
  input  b_z,
  input  alu_op_alt,
  input  [2:0] alu_op,
  input  mem_rd,
  input  mem_wr,
  input  [2:0] read_op,
  output [15:0] ex_pc,
  output [15:0] ex_next_pc,
  output [15:0] ex_Immediate,
  output ex_alu_imm,
  output ex_pc_2_alu,
  output ex_pc_from_alu,
  output ex_reg_wr,
  output [2:0] ex_rd,
  output [2:0] ex_rs1,
  output [2:0] ex_rs2,
  output ex_pc_rd,
  output ex_b_unc,
  output ex_b_nz,
  output ex_b_z,
  output ex_alu_op_alt,
  output [2:0] ex_alu_op,
  output ex_mem_rd,
  output ex_mem_wr,
  output [2:0] ex_read_op
);

  wire and_1_out, and_2_out, and_3_out, and_4_out, and_5_out, and_6_out, and_7_out, and_8_out, and_9_out,
       and_10_out, and_11_out, not_1_out, or_1_out, register_1_q;
  wire [2:0] multiplexer_4_out, multiplexer_5_out, multiplexer_6_out, multiplexer_7_out, multiplexer_8_out;
  wire [15:0] multiplexer_1_out, multiplexer_2_out, multiplexer_3_out;

  or or_1 (or_1_out, branch, register_1_q);
  Register #(.width(1)) register_1 (.D(branch), .Q(register_1_q), .clk(clk));  // open: en, clr
  Multiplexer #(.width(16), .enable("false")) multiplexer_1 (
    .in0(decode_pc), .in1({16{1'b0}}), .out(multiplexer_1_out), .sel(or_1_out));
  Multiplexer #(.width(16), .enable("false")) multiplexer_2 (
    .in0(decode_next_pc), .in1({16{1'b0}}), .out(multiplexer_2_out), .sel(or_1_out));
  Multiplexer #(.width(16), .enable("false")) multiplexer_3 (
    .in0(Immediate), .in1({16{1'b0}}), .out(multiplexer_3_out), .sel(or_1_out));
  and and_1 (and_1_out, ~or_1_out, alu_imm);  // AND_Gate
  and and_2 (and_2_out, ~or_1_out, pc_2_alu);  // AND_Gate
  and and_3 (and_3_out, ~or_1_out, pc_from_alu);  // AND_Gate
  and and_4 (and_4_out, ~or_1_out, reg_wr);  // AND_Gate
  Multiplexer #(.width(3), .enable("false")) multiplexer_4 (
    .in0(rd), .in1(3'b000), .out(multiplexer_4_out), .sel(or_1_out));
  Multiplexer #(.width(3), .enable("false")) multiplexer_5 (
    .in0(rs1), .in1(3'b000), .out(multiplexer_5_out), .sel(or_1_out));
  Multiplexer #(.width(3), .enable("false")) multiplexer_6 (
    .in0(rs2), .in1(3'b000), .out(multiplexer_6_out), .sel(or_1_out));
  and and_5 (and_5_out, ~or_1_out, pc_rd);  // AND_Gate
  and and_6 (and_6_out, ~or_1_out, b_unc);  // AND_Gate
  and and_7 (and_7_out, ~or_1_out, b_nz);  // AND_Gate
  and and_8 (and_8_out, ~or_1_out, b_z);  // AND_Gate
  and and_9 (and_9_out, ~or_1_out, alu_op_alt);  // AND_Gate
  Multiplexer #(.width(3), .enable("false")) multiplexer_7 (
    .in0(alu_op), .in1(3'b000), .out(multiplexer_7_out), .sel(or_1_out));
  and and_10 (and_10_out, ~or_1_out, mem_rd);  // AND_Gate
  and and_11 (and_11_out, ~or_1_out, mem_wr);  // AND_Gate
  Multiplexer #(.width(3), .enable("false")) multiplexer_8 (
    .in0(read_op), .in1(3'b000), .out(multiplexer_8_out), .sel(or_1_out));
  not not_1 (not_1_out, rd_mem_thn_reg_nxt);
  Register #(.width(16)) register_2 (.D(multiplexer_1_out), .en(not_1_out), .Q(ex_pc), .clk(clk), .clr(reset));
  Register #(.width(16)) register_3 (.D(multiplexer_2_out), .en(not_1_out), .Q(ex_next_pc), .clk(clk), .clr(reset));
  Register #(.width(16)) register_4 (.D(multiplexer_3_out), .en(not_1_out), .Q(ex_Immediate), .clk(clk), .clr(reset));
  Register #(.width(1)) register_5 (.D(and_1_out), .en(not_1_out), .Q(ex_alu_imm), .clk(clk), .clr(reset));
  Register #(.width(1)) register_6 (.D(and_2_out), .en(not_1_out), .Q(ex_pc_2_alu), .clk(clk), .clr(reset));
  Register #(.width(1)) register_7 (.D(and_3_out), .en(not_1_out), .Q(ex_pc_from_alu), .clk(clk), .clr(reset));
  Register #(.width(1)) register_8 (.D(and_4_out), .en(not_1_out), .Q(ex_reg_wr), .clk(clk), .clr(reset));
  Register #(.width(3)) register_9 (.D(multiplexer_4_out), .en(not_1_out), .Q(ex_rd), .clk(clk), .clr(reset));
  Register #(.width(3)) register_10 (.D(multiplexer_5_out), .en(not_1_out), .Q(ex_rs1), .clk(clk), .clr(reset));
  Register #(.width(3)) register_11 (.D(multiplexer_6_out), .en(not_1_out), .Q(ex_rs2), .clk(clk), .clr(reset));
  Register #(.width(1)) register_12 (.D(and_5_out), .en(not_1_out), .Q(ex_pc_rd), .clk(clk), .clr(reset));
  Register #(.width(1)) register_13 (.D(and_6_out), .en(not_1_out), .Q(ex_b_unc), .clk(clk), .clr(reset));
  Register #(.width(1)) register_14 (.D(and_7_out), .en(not_1_out), .Q(ex_b_nz), .clk(clk), .clr(reset));
  Register #(.width(1)) register_15 (.D(and_8_out), .en(not_1_out), .Q(ex_b_z), .clk(clk), .clr(reset));
  Register #(.width(1)) register_16 (.D(and_9_out), .en(not_1_out), .Q(ex_alu_op_alt), .clk(clk), .clr(reset));
  Register #(.width(3)) register_17 (.D(multiplexer_7_out), .en(not_1_out), .Q(ex_alu_op), .clk(clk), .clr(reset));
  Register #(.width(1)) register_18 (.D(and_10_out), .en(not_1_out), .Q(ex_mem_rd), .clk(clk), .clr(reset));
  Register #(.width(1)) register_19 (.D(and_11_out), .en(not_1_out), .Q(ex_mem_wr), .clk(clk), .clr(reset));
  Register #(.width(3)) register_20 (.D(multiplexer_8_out), .en(not_1_out), .Q(ex_read_op), .clk(clk), .clr(reset));
endmodule

// MEM_in
module Mem_Input (
  input  rd_mem_thn_reg_nxt,
  input  branch,
  input  reset,
  input  clk,
  input  [15:0] ex_pc,
  input  [15:0] ex_next_pc,
  input  [15:0] ex_Immediate,
  input  ex_alu_imm,
  input  ex_pc_2_alu,
  input  ex_pc_from_alu,
  input  ex_reg_wr,
  input  [2:0] ex_rd,
  input  [2:0] ex_rs1,
  input  [2:0] ex_rs2,
  input  ex_pc_rd,
  input  ex_b_unc,
  input  ex_b_nz,
  input  ex_b_z,
  input  ex_alu_op_alt,
  input  [2:0] ex_alu_op,
  input  ex_mem_rd,
  input  ex_mem_wr,
  input  [2:0] ex_read_op,
  output [15:0] mem_next_pc,
  output mem_pc_from_alu,
  output mem_reg_wr,
  output [2:0] mem_rd,
  output mem_pc_rd,
  output mem_b_unc,
  output mem_b_nz,
  output mem_b_z,
  output mem_mem_rd,
  output mem_mem_wr,
  output [2:0] mem_read_op
);

  wire and_1_out, and_2_out, and_3_out, and_4_out, and_5_out, and_6_out, and_7_out, and_8_out, or_1_out;
  wire [2:0] multiplexer_2_out, multiplexer_3_out;
  wire [15:0] multiplexer_1_out;

  or or_1 (or_1_out, rd_mem_thn_reg_nxt, branch);
  Multiplexer #(.width(16), .enable("false")) multiplexer_1 (
    .in0(ex_next_pc), .in1({16{1'b0}}), .out(multiplexer_1_out), .sel(or_1_out));
  and and_1 (and_1_out, ~or_1_out, ex_pc_from_alu);  // AND_Gate
  and and_2 (and_2_out, ~or_1_out, ex_reg_wr);  // AND_Gate
  Multiplexer #(.width(3), .enable("false")) multiplexer_2 (
    .in0(ex_rd), .in1(3'b000), .out(multiplexer_2_out), .sel(or_1_out));
  and and_3 (and_3_out, ~or_1_out, ex_pc_rd);  // AND_Gate
  and and_4 (and_4_out, ~or_1_out, ex_b_unc);  // AND_Gate
  and and_5 (and_5_out, ~or_1_out, ex_b_nz);  // AND_Gate
  and and_6 (and_6_out, ~or_1_out, ex_b_z);  // AND_Gate
  and and_7 (and_7_out, ~or_1_out, ex_mem_rd);  // AND_Gate
  and and_8 (and_8_out, ~or_1_out, ex_mem_wr);  // AND_Gate
  Multiplexer #(.width(3), .enable("false")) multiplexer_3 (
    .in0(ex_read_op), .in1(3'b000), .out(multiplexer_3_out), .sel(or_1_out));
  Register #(.width(16)) register_1 (.D(multiplexer_1_out), .Q(mem_next_pc), .clk(clk), .clr(reset));  // open: en
  Register #(.width(1)) register_2 (.D(and_1_out), .Q(mem_pc_from_alu), .clk(clk), .clr(reset));  // open: en
  Register #(.width(1)) register_3 (.D(and_2_out), .Q(mem_reg_wr), .clk(clk), .clr(reset));  // open: en
  Register #(.width(3)) register_4 (.D(multiplexer_2_out), .Q(mem_rd), .clk(clk), .clr(reset));  // open: en
  Register #(.width(1)) register_5 (.D(and_3_out), .Q(mem_pc_rd), .clk(clk), .clr(reset));  // open: en
  Register #(.width(1)) register_6 (.D(and_4_out), .Q(mem_b_unc), .clk(clk), .clr(reset));  // open: en
  Register #(.width(1)) register_7 (.D(and_5_out), .Q(mem_b_nz), .clk(clk), .clr(reset));  // open: en
  Register #(.width(1)) register_8 (.D(and_6_out), .Q(mem_b_z), .clk(clk), .clr(reset));  // open: en
  Register #(.width(1)) register_9 (.D(and_7_out), .Q(mem_mem_rd), .clk(clk), .clr(reset));  // open: en
  Register #(.width(1)) register_10 (.D(and_8_out), .Q(mem_mem_wr), .clk(clk), .clr(reset));  // open: en
  Register #(.width(3)) register_11 (.D(multiplexer_3_out), .Q(mem_read_op), .clk(clk), .clr(reset));  // open: en
endmodule

// WB_in
module WB_Input (
  input  branch,
  input  reset,
  input  clk,
  input  [15:0] mem_next_pc,
  input  mem_pc_from_alu,
  input  mem_reg_wr,
  input  [2:0] mem_rd,
  input  mem_pc_rd,
  input  mem_b_unc,
  input  mem_b_nz,
  input  mem_b_z,
  input  mem_mem_rd,
  output [15:0] wb_next_pc,
  output wb_pc_from_alu,
  output wb_reg_wr,
  output [2:0] wb_rd,
  output wb_pc_rd,
  output wb_b_unc,
  output wb_b_nz,
  output wb_b_z,
  output wb_mem_rd
);

  wire and_1_out, and_2_out, and_3_out, and_4_out, and_5_out, and_6_out, and_7_out;
  wire [2:0] multiplexer_2_out;
  wire [15:0] multiplexer_1_out;

  Multiplexer #(.width(16), .enable("false")) multiplexer_1 (
    .in0(mem_next_pc), .in1({16{1'b0}}), .out(multiplexer_1_out), .sel(branch));
  and and_1 (and_1_out, ~branch, mem_pc_from_alu);  // AND_Gate
  and and_2 (and_2_out, ~branch, mem_reg_wr);  // AND_Gate
  Multiplexer #(.width(3), .enable("false")) multiplexer_2 (
    .in0(mem_rd), .in1(3'b000), .out(multiplexer_2_out), .sel(branch));
  and and_3 (and_3_out, ~branch, mem_pc_rd);  // AND_Gate
  and and_4 (and_4_out, ~branch, mem_b_unc);  // AND_Gate
  and and_5 (and_5_out, ~branch, mem_b_nz);  // AND_Gate
  and and_6 (and_6_out, ~branch, mem_b_z);  // AND_Gate
  and and_7 (and_7_out, ~branch, mem_mem_rd);  // AND_Gate
  Register #(.width(16)) register_1 (.D(multiplexer_1_out), .Q(wb_next_pc), .clk(clk), .clr(reset));  // open: en
  Register #(.width(1)) register_2 (.D(and_1_out), .Q(wb_pc_from_alu), .clk(clk), .clr(reset));  // open: en
  Register #(.width(1)) register_3 (.D(and_2_out), .Q(wb_reg_wr), .clk(clk), .clr(reset));  // open: en
  Register #(.width(3)) register_4 (.D(multiplexer_2_out), .Q(wb_rd), .clk(clk), .clr(reset));  // open: en
  Register #(.width(1)) register_5 (.D(and_3_out), .Q(wb_pc_rd), .clk(clk), .clr(reset));  // open: en
  Register #(.width(1)) register_6 (.D(and_4_out), .Q(wb_b_unc), .clk(clk), .clr(reset));  // open: en
  Register #(.width(1)) register_7 (.D(and_5_out), .Q(wb_b_nz), .clk(clk), .clr(reset));  // open: en
  Register #(.width(1)) register_8 (.D(and_6_out), .Q(wb_b_z), .clk(clk), .clr(reset));  // open: en
  Register #(.width(1)) register_9 (.D(and_7_out), .Q(wb_mem_rd), .clk(clk), .clr(reset));  // open: en
endmodule

// WB_ALU
module WB_ALU_input (
  input  clk,
  input  reset,
  input  [15:0] ALU_out,
  input  Zero,
  output [15:0] wb_alu_input,
  output wb_zero
);

  Register #(.width(16)) register_1 (.D(ALU_out), .Q(wb_alu_input), .clk(clk), .clr(reset));  // open: en
  Register #(.width(1)) register_2 (.D(Zero), .Q(wb_zero), .clk(clk), .clr(reset));  // open: en
endmodule

// WB
module Writeback (
  input  [15:0] wb_next_pc,
  input  wb_pc_from_alu,
  input  wb_reg_wr,
  input  [2:0] wb_rd,
  input  wb_pc_rd,
  input  wb_b_unc,
  input  wb_b_nz,
  input  wb_b_z,
  input  wb_mem_rd,
  input  [15:0] wb_alu,
  input  wb_zero,
  input  [15:0] mem_rd,
  output [15:0] register_data,
  output branch
);

  wire and_1_out, and_2_out;
  wire [15:0] multiplexer_1_out;

  and and_1 (and_1_out, wb_b_nz, ~wb_zero);  // AND_Gate
  and and_2 (and_2_out, wb_zero, wb_b_z);
  Multiplexer #(.width(16), .enable("false")) multiplexer_1 (
    .in0(wb_alu), .in1(mem_rd), .out(multiplexer_1_out), .sel(wb_mem_rd));
  or or_1 (branch, wb_b_unc, and_1_out, and_2_out);
  Multiplexer #(.width(16), .enable("false")) multiplexer_2 (
    .in0(multiplexer_1_out), .in1(wb_next_pc), .out(register_data), .sel(wb_pc_rd));
endmodule

module CPU_Pipelined (
  input  halted,
  input  reset,
  input  clk,
  input  [15:0] Instruction,
  input  [15:0] mem_read,
  output read_instruction,
  output [15:0] PC,
  output [15:0] mem_addr,
  output [15:0] mem_wr,
  output wr,
  output rd
);

  wire alu_pipelined_1_zero, ex_input_1_ex_alu_imm, ex_input_1_ex_alu_op_alt, ex_input_1_ex_b_nz,
       ex_input_1_ex_b_unc, ex_input_1_ex_b_z, ex_input_1_ex_mem_rd, ex_input_1_ex_mem_wr,
       ex_input_1_ex_pc_2_alu, ex_input_1_ex_pc_from_alu, ex_input_1_ex_pc_rd, ex_input_1_ex_reg_wr,
       instruction_decode_1_alu_imm, instruction_decode_1_alu_op_alt, instruction_decode_1_b_nz,
       instruction_decode_1_b_unc, instruction_decode_1_b_z, instruction_decode_1_halt,
       instruction_decode_1_mem_rd, instruction_decode_1_mem_wr, instruction_decode_1_pc_2_alu,
       instruction_decode_1_pc_from_alu, instruction_decode_1_pc_rd, instruction_decode_1_reg_wr,
       mem2reg_out, mem_input_1_mem_b_nz, mem_input_1_mem_b_unc, mem_input_1_mem_b_z, mem_input_1_mem_mem_rd,
       mem_input_1_mem_mem_wr, mem_input_1_mem_pc_from_alu, mem_input_1_mem_pc_rd, mem_input_1_mem_reg_wr,
       nand_1_out, not_1_out, not_2_out, not_3_out, or_1_out, or_2_out, or_3_out, or_4_out,
       rs_rd_rs_0_1_mem_cond, rs_rd_rs_0_2_mem_cond, upd_out, wb_alu_input_1_wb_zero, wb_input_1_wb_b_nz,
       wb_input_1_wb_b_unc, wb_input_1_wb_b_z, wb_input_1_wb_mem_rd, wb_input_1_wb_pc_from_alu,
       wb_input_1_wb_pc_rd, wb_input_1_wb_reg_wr, writeback_1_branch;
  wire [1:0] mem_input_1_mem_read_op, rs_rd_rs_0_3_mem_cond, rs_rd_rs_0_5_mem_cond;
  wire [1:1] mem_input_1_mem_read_op_2;
  wire [2:0] ex_input_1_ex_alu_op, ex_input_1_ex_rd, ex_input_1_ex_read_op, ex_input_1_ex_rs1,
       ex_input_1_ex_rs2, instruction_decode_1_alu_op, instruction_decode_1_rd, instruction_decode_1_read_op,
       instruction_decode_1_rs1, instruction_decode_1_rs2, mem_input_1_mem_rd, wb_input_1_wb_rd;
  wire [15:0] add_16bit_pc_1_s, bit_extender_1_out, bit_extender_2_out, bit_extender_3_out,
       ex_input_1_ex_immediate, ex_input_1_ex_next_pc, ex_input_1_ex_pc, instruction_decode_1_immediate,
       mem_input_1_mem_next_pc, multiplexer_1_out, multiplexer_2_out, multiplexer_3_out, multiplexer_4_out,
       multiplexer_5_out, multiplexer_6_out, multiplexer_7_out, pc_decode_1_decode_next_pc,
       pc_decode_1_decode_pc, pc_pipelined_1_next_pc, register_1_q, register_2_q, register_3_q, register_4_q,
       registers_pipelined_1_r1_d, registers_pipelined_1_r2_d, wb_alu_input_1_wb_alu_input,
       wb_input_1_wb_next_pc, writeback_1_register_data;

  or or_1 (or_1_out, halted, instruction_decode_1_halt);
  and upd (upd_out, ~or_1_out, or_3_out);  // AND_Gate
  PC_pipelined pc_pipelined_1 (
    .clk(clk), .reset(reset), .update(upd_out), .branch(writeback_1_branch), .branch_pc(multiplexer_5_out),
    .pc(PC), .next_pc(pc_pipelined_1_next_pc));
  PC_decode pc_decode_1 (
    .pc(PC), .next_pc(pc_pipelined_1_next_pc), .clk(clk), .reset(reset), .decode_pc(pc_decode_1_decode_pc),
    .decode_next_pc(pc_decode_1_decode_next_pc));
  Instruction_Decode instruction_decode_1 (
    .halt(instruction_decode_1_halt), .Instruction(Instruction), .Immediate(instruction_decode_1_immediate),
    .alu_imm(instruction_decode_1_alu_imm), .pc_2_alu(instruction_decode_1_pc_2_alu),
    .pc_from_alu(instruction_decode_1_pc_from_alu), .reg_wr(instruction_decode_1_reg_wr),
    .rd(instruction_decode_1_rd), .rs1(instruction_decode_1_rs1), .rs2(instruction_decode_1_rs2),
    .pc_rd(instruction_decode_1_pc_rd), .b_unc(instruction_decode_1_b_unc), .b_nz(instruction_decode_1_b_nz),
    .b_z(instruction_decode_1_b_z), .alu_op_alt(instruction_decode_1_alu_op_alt),
    .alu_op(instruction_decode_1_alu_op), .mem_rd(instruction_decode_1_mem_rd),
    .mem_wr(instruction_decode_1_mem_wr), .read_op(instruction_decode_1_read_op));
  rs_rd_rs__0 rs_rd_rs_0_1 (.mem_cond(rs_rd_rs_0_1_mem_cond), .rs(instruction_decode_1_rs2), .rd(ex_input_1_ex_rd));
  Registers_pipelined registers_pipelined_1 (
    .rd_a(wb_input_1_wb_rd), .r1_a(instruction_decode_1_rs1), .r2_a(instruction_decode_1_rs2),
    .wr(writeback_1_register_data), .reg_wr(wb_input_1_wb_reg_wr), .clk(clk), .reset(reset),
    .r1_d(registers_pipelined_1_r1_d), .r2_d(registers_pipelined_1_r2_d));
  Ex_Input ex_input_1 (
    .clk(clk), .decode_pc(pc_decode_1_decode_pc), .decode_next_pc(pc_decode_1_decode_next_pc),
    .Immediate(instruction_decode_1_immediate), .alu_imm(instruction_decode_1_alu_imm),
    .pc_2_alu(instruction_decode_1_pc_2_alu), .pc_from_alu(instruction_decode_1_pc_from_alu),
    .reg_wr(instruction_decode_1_reg_wr), .rd(instruction_decode_1_rd), .rs1(instruction_decode_1_rs1),
    .rs2(instruction_decode_1_rs2), .pc_rd(instruction_decode_1_pc_rd), .b_unc(instruction_decode_1_b_unc),
    .b_nz(instruction_decode_1_b_nz), .b_z(instruction_decode_1_b_z),
    .alu_op_alt(instruction_decode_1_alu_op_alt), .alu_op(instruction_decode_1_alu_op),
    .mem_rd(instruction_decode_1_mem_rd), .mem_wr(instruction_decode_1_mem_wr),
    .read_op(instruction_decode_1_read_op), .branch(writeback_1_branch), .rd_mem_thn_reg_nxt(mem2reg_out),
    .reset(reset), .ex_pc(ex_input_1_ex_pc), .ex_next_pc(ex_input_1_ex_next_pc),
    .ex_Immediate(ex_input_1_ex_immediate), .ex_alu_imm(ex_input_1_ex_alu_imm),
    .ex_pc_2_alu(ex_input_1_ex_pc_2_alu), .ex_pc_from_alu(ex_input_1_ex_pc_from_alu),
    .ex_reg_wr(ex_input_1_ex_reg_wr), .ex_rd(ex_input_1_ex_rd), .ex_rs1(ex_input_1_ex_rs1),
    .ex_rs2(ex_input_1_ex_rs2), .ex_pc_rd(ex_input_1_ex_pc_rd), .ex_b_unc(ex_input_1_ex_b_unc),
    .ex_b_nz(ex_input_1_ex_b_nz), .ex_b_z(ex_input_1_ex_b_z), .ex_alu_op_alt(ex_input_1_ex_alu_op_alt),
    .ex_alu_op(ex_input_1_ex_alu_op), .ex_mem_rd(ex_input_1_ex_mem_rd), .ex_mem_wr(ex_input_1_ex_mem_wr),
    .ex_read_op(ex_input_1_ex_read_op));
  rs_rd_rs__0 rs_rd_rs_0_2 (.mem_cond(rs_rd_rs_0_2_mem_cond), .rs(instruction_decode_1_rs1), .rd(ex_input_1_ex_rd));
  or or_2 (or_2_out, rs_rd_rs_0_1_mem_cond, rs_rd_rs_0_2_mem_cond);
  or or_3 (or_3_out, nand_1_out, writeback_1_branch);
  nand nand_1 (nand_1_out, or_2_out, ex_input_1_ex_mem_rd);
  Multiplexer #(.select(2), .width(16), .enable("false")) multiplexer_1 (
    .in0(registers_pipelined_1_r1_d), .in1(writeback_1_register_data), .in2(mem_addr), .in3({16{1'b0}}),
    .out(multiplexer_1_out), .sel(rs_rd_rs_0_3_mem_cond));
  rs_rd_rs__0 rs_rd_rs_0_3 (.mem_cond(rs_rd_rs_0_3_mem_cond[0]), .rs(ex_input_1_ex_rs1), .rd(wb_input_1_wb_rd));
  rs_rd_rs__0 rs_rd_rs_0_4 (.mem_cond(rs_rd_rs_0_3_mem_cond[1]), .rs(ex_input_1_ex_rs1), .rd(mem_input_1_mem_rd));
  not not_1 (not_1_out, ex_input_1_ex_alu_imm);
  Multiplexer #(.select(2), .width(16), .enable("false")) multiplexer_2 (
    .in0(registers_pipelined_1_r2_d), .in1(writeback_1_register_data), .in2(mem_addr), .in3({16{1'b0}}),
    .out(multiplexer_2_out), .sel(rs_rd_rs_0_5_mem_cond));
  rs_rd_rs__0 rs_rd_rs_0_5 (.mem_cond(rs_rd_rs_0_5_mem_cond[0]), .rs(ex_input_1_ex_rs2), .rd(wb_input_1_wb_rd));
  rs_rd_rs__0 rs_rd_rs_0_6 (.mem_cond(rs_rd_rs_0_5_mem_cond[1]), .rs(ex_input_1_ex_rs2), .rd(mem_input_1_mem_rd));
  add_16bit_pc add_16bit_pc_1 (.A(ex_input_1_ex_pc), .B(ex_input_1_ex_immediate), .S(add_16bit_pc_1_s));
  Register #(.width(16)) register_1 (.D(add_16bit_pc_1_s), .Q(register_1_q), .clk(clk), .clr(reset));  // open: en
  not not_2 (not_2_out, ex_input_1_ex_pc_2_alu);
  Multiplexer #(.width(16), .enable("false")) multiplexer_3 (
    .in0(ex_input_1_ex_pc), .in1(multiplexer_1_out), .out(multiplexer_3_out), .sel(not_2_out));
  Multiplexer #(.width(16), .enable("false")) multiplexer_4 (
    .in0(ex_input_1_ex_immediate), .in1(multiplexer_2_out), .out(multiplexer_4_out), .sel(not_1_out));
  Mem_Input mem_input_1 (
    .clk(clk), .ex_pc(ex_input_1_ex_pc), .ex_next_pc(ex_input_1_ex_next_pc),
    .ex_Immediate(ex_input_1_ex_immediate), .ex_alu_imm(ex_input_1_ex_alu_imm),
    .ex_pc_2_alu(ex_input_1_ex_pc_2_alu), .ex_pc_from_alu(ex_input_1_ex_pc_from_alu),
    .ex_reg_wr(ex_input_1_ex_reg_wr), .ex_rd(ex_input_1_ex_rd), .ex_rs1(ex_input_1_ex_rs1),
    .ex_rs2(ex_input_1_ex_rs2), .ex_pc_rd(ex_input_1_ex_pc_rd), .ex_b_unc(ex_input_1_ex_b_unc),
    .ex_b_nz(ex_input_1_ex_b_nz), .ex_b_z(ex_input_1_ex_b_z), .ex_alu_op_alt(ex_input_1_ex_alu_op_alt),
    .ex_alu_op(ex_input_1_ex_alu_op), .ex_mem_rd(ex_input_1_ex_mem_rd), .ex_mem_wr(ex_input_1_ex_mem_wr),
    .ex_read_op(ex_input_1_ex_read_op), .rd_mem_thn_reg_nxt(mem2reg_out), .branch(writeback_1_branch),
    .reset(reset), .mem_next_pc(mem_input_1_mem_next_pc), .mem_pc_from_alu(mem_input_1_mem_pc_from_alu),
    .mem_reg_wr(mem_input_1_mem_reg_wr), .mem_rd(mem_input_1_mem_rd), .mem_pc_rd(mem_input_1_mem_pc_rd),
    .mem_b_unc(mem_input_1_mem_b_unc), .mem_b_nz(mem_input_1_mem_b_nz), .mem_b_z(mem_input_1_mem_b_z),
    .mem_mem_rd(mem_input_1_mem_mem_rd), .mem_mem_wr(mem_input_1_mem_mem_wr),
    .mem_read_op({mem_input_1_mem_read_op[1], mem_input_1_mem_read_op_2[1], mem_input_1_mem_read_op[0]}));
  ALU_pipelined alu_pipelined_1 (
    .op_alt(ex_input_1_ex_alu_op_alt), .op(ex_input_1_ex_alu_op), .A(multiplexer_3_out),
    .B(multiplexer_4_out), .clk(clk), .reset(reset), .ALU_out(mem_addr), .Zero(alu_pipelined_1_zero));
  and mem2reg (mem2reg_out, or_4_out, mem_input_1_mem_mem_rd);
  or or_4 (or_4_out, rs_rd_rs_0_3_mem_cond[1], rs_rd_rs_0_5_mem_cond[0]);
  and u_wr (wr, mem_input_1_mem_mem_wr, ~writeback_1_branch);  // AND_Gate
  and u_rd (rd, ~writeback_1_branch, mem_input_1_mem_mem_rd);  // AND_Gate
  Register #(.width(16)) register_2 (.D(register_1_q), .Q(register_2_q), .clk(clk), .clr(reset));  // open: en
  WB_ALU_input wb_alu_input_1 (
    .ALU_out(mem_addr), .Zero(alu_pipelined_1_zero), .clk(clk), .reset(reset),
    .wb_alu_input(wb_alu_input_1_wb_alu_input), .wb_zero(wb_alu_input_1_wb_zero));
  Multiplexer #(.width(16), .enable("false")) multiplexer_5 (
    .in0(register_2_q), .in1(wb_alu_input_1_wb_alu_input), .out(multiplexer_5_out),
    .sel(wb_input_1_wb_pc_from_alu));
  WB_Input wb_input_1 (
    .clk(clk), .mem_next_pc(mem_input_1_mem_next_pc), .mem_pc_from_alu(mem_input_1_mem_pc_from_alu),
    .mem_reg_wr(mem_input_1_mem_reg_wr), .mem_rd(mem_input_1_mem_rd), .mem_pc_rd(mem_input_1_mem_pc_rd),
    .mem_b_unc(mem_input_1_mem_b_unc), .mem_b_nz(mem_input_1_mem_b_nz), .mem_b_z(mem_input_1_mem_b_z),
    .mem_mem_rd(mem_input_1_mem_mem_rd), .branch(writeback_1_branch), .reset(reset),
    .wb_next_pc(wb_input_1_wb_next_pc), .wb_pc_from_alu(wb_input_1_wb_pc_from_alu),
    .wb_reg_wr(wb_input_1_wb_reg_wr), .wb_rd(wb_input_1_wb_rd), .wb_pc_rd(wb_input_1_wb_pc_rd),
    .wb_b_unc(wb_input_1_wb_b_unc), .wb_b_nz(wb_input_1_wb_b_nz), .wb_b_z(wb_input_1_wb_b_z),
    .wb_mem_rd(wb_input_1_wb_mem_rd));
  Writeback writeback_1 (
    .wb_next_pc(wb_input_1_wb_next_pc), .wb_pc_from_alu(wb_input_1_wb_pc_from_alu),
    .wb_reg_wr(wb_input_1_wb_reg_wr), .wb_rd(wb_input_1_wb_rd), .wb_pc_rd(wb_input_1_wb_pc_rd),
    .wb_b_unc(wb_input_1_wb_b_unc), .wb_b_nz(wb_input_1_wb_b_nz), .wb_b_z(wb_input_1_wb_b_z),
    .wb_mem_rd(wb_input_1_wb_mem_rd), .wb_alu(wb_alu_input_1_wb_alu_input), .wb_zero(wb_alu_input_1_wb_zero),
    .mem_rd(register_4_q), .register_data(writeback_1_register_data), .branch(writeback_1_branch));
  not not_3 (not_3_out, rs_rd_rs_0_5_mem_cond[0]);
  Multiplexer #(.width(16), .enable("false")) multiplexer_6 (
    .in0(mem_addr), .in1(registers_pipelined_1_r2_d), .out(multiplexer_6_out), .sel(not_3_out));
  Register #(.width(16)) register_3 (.D(multiplexer_6_out), .Q(register_3_q), .clk(clk), .clr(reset));  // open: en
  Register #(.width(16)) register_4 (.D(multiplexer_7_out), .Q(register_4_q), .clk(clk), .clr(reset));  // open: en
  nor nor_1 (read_instruction, or_1_out, reset);
  assign bit_extender_1_out = {{8{mem_read[7]}}, mem_read[7:0]};  // Bit_Extender bit_extender_1
  assign bit_extender_2_out = {{8{1'b0}}, mem_read[7:0]};  // Bit_Extender bit_extender_2
  assign bit_extender_3_out = {{8{1'b0}}, register_3_q[7:0]};  // Bit_Extender bit_extender_3
  Multiplexer #(.select(2), .width(16), .disabled(0), .enable("false")) multiplexer_7 (
    .in0(bit_extender_1_out), .in1(mem_read), .in2(bit_extender_2_out), .in3(mem_read),
    .out(multiplexer_7_out), .sel(mem_input_1_mem_read_op));
  Multiplexer #(.width(16), .disabled(0), .enable("false")) multiplexer_8 (
    .in0(bit_extender_3_out), .in1(register_3_q), .out(mem_wr), .sel(mem_input_1_mem_read_op[0]));
endmodule

module main_pipe (
  input  halted,
  input  reset,
  output read_instr
);

  wire clock_1_out, cpu_pipelined_1_rd, cpu_pipelined_1_wr;
  wire [7:0] cpu_pipelined_1_pc_2;
  wire [15:0] cpu_pipelined_1_mem_addr, cpu_pipelined_1_mem_wr, cpu_pipelined_1_pc, ram_1_data, rom_1_data;

  Clock clock_1 (.out(clock_1_out));
  ROM #(.dataWidth(16)) rom_1 (.addr(cpu_pipelined_1_pc_2), .data(rom_1_data));  // open: sel
  CPU_Pipelined cpu_pipelined_1 (
    .halted(halted), .reset(reset), .clk(clock_1_out), .Instruction(rom_1_data),
    .PC({cpu_pipelined_1_pc[15:9], cpu_pipelined_1_pc_2, cpu_pipelined_1_pc[0]}),
    .read_instruction(read_instr), .mem_addr(cpu_pipelined_1_mem_addr), .mem_wr(cpu_pipelined_1_mem_wr),
    .mem_read(ram_1_data), .wr(cpu_pipelined_1_wr), .rd(cpu_pipelined_1_rd));
  RAM #(.dataWidth(16), .bus("separate")) ram_1 (
    .addr(cpu_pipelined_1_mem_addr[7:0]), .din(cpu_pipelined_1_mem_wr), .data(ram_1_data),
    .str(cpu_pipelined_1_wr), .clk(clock_1_out), .ld(cpu_pipelined_1_rd), .clr(reset));  // open: sel

  // Notes on the sheet:
  //   contents of rom_1 (hex, n*v repeats v):
  //   5038 5858 1170 8a90 11b7 11d6 11f4 1807 5 2108 ea22 5258 be62 7378
endmodule
